# Fritzing sketch Imperfect_Scorpion (saved by Fritzing 1.0.0d)

parts:
  L298N1 = L298N DC motor driver
  U1 = LuaNode32 / ESP32 [part_number=ESP32S-PIN30]
  M1 = DC Motor [voltage_(max)=6V voltage_(min)=3V]
  M2 = Dagu DGServo 9g (Pan and tilt) [part_number=RS001B]
  BAT1 = 18650 battery holder [package=battery-18650-kit]
  BAT2 = 18650 battery holder [package=battery-18650-kit]

nets:
  N1: L298N1.OUT1, M1.pin_2
  N2: L298N1.OUT2, M1.pin_1
  N3: L298N1.12V, BAT1.+
  GND: L298N1.GND, U1.GND, M2.gnd, BAT2.-
  5V: L298N1.5V, U1.Vin, M2.vcc
  N4: L298N1.ENA, U1.D14
  N5: L298N1.IN1, U1.D27
  N6: L298N1.IN2, U1.D26
  N7: U1.D33, M2.pulse
  N8: BAT1.-, BAT2.+

custom parts:
  L298N DC motor driver: 2x DC motor driver with 78M05 positive voltage regulator (7..35 V) L298N: max 46 V, 2 A Set 5 V Enable jumper to enable 5 V regultor (needed for the L298N) and +5 V output at screw terminal or supply external +5 V at screw terminal Set ENA and/or ENB to +5 V to enable motor permanently or supply ENA and/or ENB with PWM signal IN1 and IN2 set rotation directory for motor A (OUT1/OUT2) IN2 and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
  LuaNode32 / ESP32: New Image for LuaNode32 DOIT ESP32 DEVKIT V1. Base parts from LuaNode32 / ESP32 ESP32 based LuaNode32 by G.Noorlander DOIT Esp32 DevKit v1 (30 pins long, 11 pins width) by Werner Rothschopf (modified by vanepp Dec 2018)
  18650 battery holder: 18650 Battery Holder
